# Fritzing sketch BreadboardOverview (saved by Fritzing 0.9.10b)
breadboards: 1

parts:
  M1 = Arduino MKR WAN 1300
  ANT1 = Antenna  # not connected
  RHT1 = Humidity and Temperature Sensor RHT03
  S1 = KY-026
  Part1 = NeoPixel Stick [part_number=1426]
  U1 = LIPO-1000mAh [package=lipo-1000]
  Part2 = Adafruit BQ24074 Solar-DC-USB Lipo Charger
  Part3 = Solar Panel [package="Renogy 50 Watts 12 Volt Monocrystalline Bendable Solar Panel"]  # not connected

nets:
  N1: M1.~2, Part1.DATAOUT
  N2: M1.~4, S1.pin4
  N3: M1.~5, RHT1.Data-signal
  GND: M1.GND, RHT1.GND_1, S1.pin2, Part1.GND
  5V: M1.5V, RHT1.Vcc, S1.pin3, Part1.+5V
  N4: U1.+, Part2.VLIPO
  N5: U1.-, Part2.GND

custom parts:
  Arduino MKR WAN 1300: Arduino MKR WAN 1300 ,Cortex-M0 CPU with LoRa connectivity. CPU: SAMD21 Cortex-M0+ 32bit low power ARM MCU, 256 KB Flash 32K SRAM. Note: pins 28 and 29 (-VBAT and +VBAT) aren't defined in PCB view, because they are terminal blocks and don't connect to the pcb. Parts Editor will complain about unassigned pins but it is safe to ignore those 2 pins.
  KY-026: ky-026 flame sensor module
  NeoPixel Stick: Make your own little LED strip arrangement with this stick of NeoPixel LEDs. We crammed 8 of the tiny 5050 (5mm x 5mm) smart RGB LEDs onto a PCB with mounting holes and a chainable design. Use only one microcontroller pin to control as many as you can chain together! Each LED is addressable as the driver chip is inside the LED. Each one has ~18mA constant current drive so the color will be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
  Solar Panel: Renogy 50 Watts 12 Volt Solar Panel
